# Fritzing sketch AtticFanController (saved by Fritzing 0.9.4)
breadboards: 1

parts:
  Argon1 = Particle Argon
  SONGLE_Relay = Keyes Relay [package=THT]
  OLED_I2C1 = OLED 128x64 I2C Monochrome Display
  BME_280 = BMP280
  R1--100_Ω = Resistor [tolerance=±5% resistance=220 package="1206 [SMD]"]
  E_B_C = PNP-Transistor [package="TO92 [THT]"]
  S1 = Pushbutton [package="[THT]"]
  S3 = Pushbutton [package="[THT]"]
  R2--2_2k_Ω = Resistor [tolerance=±5% resistance=220 package=THT]
  FURNACE_OUTLET = JST-B3P-VH [part_number=JST-B3P-VH package=THT]  # not connected

nets:
  3.3V: Argon1.3.3V, Argon1.RX, Argon1.D3, SONGLE_Relay.power, OLED_I2C1.VDD, BME_280.VIN, S1.Pin_1, S1.Pin_2, S1.Pin_3, S1.Pin_4, S3.Pin_3, S3.Pin_4
  GND: Argon1.GND, Argon1.D2, SONGLE_Relay.ground, OLED_I2C1.GND, BME_280.GND, E_B_C.C, R2--2_2k_Ω.Pin_1
  N1: Argon1.TX, S3.Pin_1, S3.Pin_2
  N2: Argon1.SDA, OLED_I2C1.SDA, BME_280.SDA
  N3: Argon1.SCL, OLED_I2C1.SCK, BME_280.SCL
  N4: Argon1.D7, E_B_C.B, R2--2_2k_Ω.Pin_0
  N5: Argon1.VUSB, R1--100_Ω.Pin_0
  N6: SONGLE_Relay.signal, R1--100_Ω.Pin_1, E_B_C.E
  N7: SONGLE_Relay.NC, SONGLE_Relay.C, SONGLE_Relay.NO

notes:
  ATTIC FAN

custom parts:
  Particle Argon: The Argon is a powerful Wi-Fi enabled development board that can act as either a standalone Wi-Fi endpoint or Wi-Fi enabled gateway for Particle Mesh networks. It is based on the Nordic nRF52840 and has built-in battery charging circuitry so it’s easy to connect a Li-Po and deploy your local network in minutes. The Argon is great for connecting existing projects to the Particle Device Cloud or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
  Keyes Relay: The Keyes 5V relay module is suitable for SCM development, home appliance control. It uses a 5V~12V TIL control signal which can control DC / AC signal.
  BMP280: Temperature Humidity Barometric presure Sensor, I2C
  Pushbutton: A generic pushbutton.
  Pushbutton: A generic pushbutton.
